// Logisim project mycpu.circ as structural Verilog: 8 circuits, main circuit main
module main (
  input  in_1,
  output [31:0] out_2,
  output [31:0] out_3,
  output out_4,
  output [4:0] out_5,
  output [31:0] out_6,
  output out_7,
  output [31:0] out_8,
  output halt,
  output [31:0] out_10
);

  wire clk, clock_1_out, clock_2_out, comparator_1_eq, comparator_1_lt, ctrl_1_alusrc, ctrl_1_beq,
       ctrl_1_memtoreg, ctrl_1_regdst, EXTOp, JAL, nor_1_out, zero;
  wire [1:0] ctrl_1_aluop, ctrl_1_regwrop, npcop_1_npcop;
  wire [4:0] multiplexer_1_out;
  wire [11:0] counter_1_q;
  wire [31:0] dm_1_rd, grf_1_out_8, imm32, multiplexer_4_out, PC_4, RegData;

  NPCOp npcop_1 (.BEQ(ctrl_1_beq), .zero(zero), .JAL(JAL), .NPCOp(npcop_1_npcop));
  IFU ifu_1 (
    .clk(clk), .rst(in_1), .inStr(out_2), .NPCOp(npcop_1_npcop), .out_8(out_3), .imm(imm32),
    .instr_index(out_2[25:0]), .PC_4(PC_4));
  CTRL ctrl_1 (
    .op(out_2[31:26]), .func(out_2[5:0]), .RegDst(ctrl_1_regdst), .ALUOp(ctrl_1_aluop),
    .ALUSrc(ctrl_1_alusrc), .RegWr(out_4), .MemWr(out_7), .beq(ctrl_1_beq), .MemToReg(ctrl_1_memtoreg),
    .EXTOp(EXTOp), .RegWrOp(ctrl_1_regwrop), .JAL(JAL));
  Multiplexer #(.width(5)) multiplexer_1 (
    .in0(out_2[20:16]), .in1(out_2[15:11]), .out(multiplexer_1_out), .sel(ctrl_1_regdst));  // open: en
  Clock clock_1 (.out(clock_1_out));
  Multiplexer #(.select(2), .width(32)) multiplexer_2 (
    .in0(RegData), .in1({out_2[15:0], {16{1'b0}}}), .in2(PC_4), .out(out_6), .sel(ctrl_1_regwrop));  // open: in3, en
  Multiplexer #(.width(5)) multiplexer_3 (
    .in0(multiplexer_1_out), .in1({5{1'b1}}), .out(out_5), .sel(JAL));  // open: en
  Counter #(.width(12), .max('hfff), .ongoal("stay")) counter_1 (
    .D(12'h1), .Q(counter_1_q), .clk(clock_1_out));  // open: load, count, carry, clr
  EXT ext_1 (.in_2(out_2[15:0]), .out_3(imm32), .EXTOp(EXTOp));
  Comparator #(.width(12)) comparator_1 (
    .a(12'h300), .b(counter_1_q), .eq(comparator_1_eq), .lt(comparator_1_lt));  // open: gt
  GRF grf_1 (
    .A1(out_2[25:21]), .A2(out_2[20:16]), .A3(out_5), .WD(out_6), .out_8(grf_1_out_8), .out_9(out_10),
    .clk(clk), .reset(in_1), .WE(out_4));
  Counter #(.width(1), .max('h1), .ongoal("stay")) counter_2 (
    .D(1'b1), .Q(halt), .clk(clock_2_out), .clr(nor_1_out));  // open: load, count, carry
  Clock clock_2 (.out(clock_2_out));
  nor nor_1 (nor_1_out, comparator_1_eq, comparator_1_lt);
  Multiplexer #(.width(32)) multiplexer_4 (
    .in0(out_10), .in1(imm32), .out(multiplexer_4_out), .sel(ctrl_1_alusrc));  // open: en
  ALU alu_1 (.SrcA(grf_1_out_8), .SrcB(multiplexer_4_out), .out_5(out_8), .ALUOp(ctrl_1_aluop), .zero(zero));
  Multiplexer #(.width(32)) multiplexer_5 (
    .in0(out_8), .in1(dm_1_rd), .out(RegData), .sel(ctrl_1_memtoreg));  // open: en
  DM dm_1 (.Address(out_8), .WD(out_10), .clk(clk), .reset(in_1), .MemWrite(out_7), .RD(dm_1_rd));
  Clock clock_3 (.out(clk));

  // Other names for the same wires on the sheet: imm16[15:0] = out_2[15:0]; Instr[31:0] = out_2;
  //   instr_index[25:0] = out_2[25:0]; MemAddr[31:0] = out_8; MemData[31:0] = out_10; MemWr = out_7; PC[31:0] = out_3;
  //   RegAddr[4:0] = out_5; RegWr = out_4; RegWrData[31:0] = out_6; rst = in_1

  // Notes on the sheet:
  //   op
  //   funct
  //   rd
  //   RegDst
  //   rs
  //   R1
  //   rt
  //   R2
  //   W
  //   WD
  //   RegWrOp
  //   RD1
  //   RD2
  //   ALUSrc
  //   ALUOp
  //   WE
  //   A
  //   RD
  //   WD
  //   rst
  //   MemToReg
endmodule

module CTRL (
  input  [5:0] op,
  input  [5:0] func,
  output RegDst,
  output [1:0] ALUOp,
  output ALUSrc,
  output RegWr,
  output [1:0] RegWrOp,
  output MemWr,
  output beq,
  output MemToReg,
  output EXTOp,
  output JAL
);

  wire ADD, add_out, BEQ_t, LUI, LW, not_1_out, not_2_out, not_3_out, not_4_out, not_5_out, not_6_out,
       not_7_out, not_8_out, not_9_out, not_10_out, not_11_out, not_12_out, or_out, ORI, R, sll_out, SUB,
       sub_out, SW, undriven;

  not not_1 (not_1_out, op[5]);
  not not_2 (not_2_out, op[4]);
  not not_3 (not_3_out, op[2]);
  not not_4 (not_4_out, op[3]);
  not not_5 (not_5_out, op[1]);
  not not_6 (not_6_out, op[0]);
  not not_7 (not_7_out, func[4]);
  not not_8 (not_8_out, func[5]);
  not not_9 (not_9_out, func[3]);
  not not_10 (not_10_out, func[2]);
  not not_11 (not_11_out, func[0]);
  not not_12 (not_12_out, func[1]);
  and and_1 (R, not_6_out, not_5_out, not_3_out, not_4_out, not_2_out, not_1_out);
  and and_2 (ADD, R, not_11_out, not_12_out, not_10_out, not_9_out, not_7_out, func[5]);
  and and_3 (SUB, R, not_11_out, func[1], not_10_out, not_9_out, not_7_out, func[5]);
  and and_4 (ORI, op[0], not_5_out, op[2], op[3], not_2_out, not_1_out);
  and and_5 (LW, op[0], op[1], not_3_out, not_4_out, not_2_out, op[5]);
  and and_6 (SW, op[0], op[1], not_3_out, op[3], not_2_out, op[5]);
  and and_7 (BEQ_t, not_6_out, not_5_out, op[2], not_4_out, not_2_out, not_1_out);
  and and_8 (LUI, op[0], op[1], op[2], op[3], not_2_out, not_1_out);
  and and_9 (JAL, op[0], op[1], not_3_out, not_4_out, not_2_out, not_1_out);
  or u_add (add_out, ADD, LW, SW);
  or u_sub (sub_out, SUB, BEQ_t);
  buf \or  (or_out, ORI);  // OR_Gate
  buf sll (sll_out, undriven);  // OR_Gate
  or _1 (ALUSrc, ORI, LW, SW);
  or or_2 (RegWrOp[0], 1'b0, LUI);
  or or_3 (RegDst, ADD, SUB);
  or _1_2 (RegWr, ADD, SUB, ORI, LW, LUI, JAL);
  buf _1_3 (MemWr, SW);  // OR_Gate
  buf _1_4 (beq, BEQ_t);  // OR_Gate
  buf _1_5 (MemToReg, LW);  // OR_Gate
  or _1_6 (EXTOp, LW, SW, BEQ_t);
  buf _0 (ALUOp[0], sub_out);  // OR_Gate
  buf _1_7 (ALUOp[1], or_out);  // OR_Gate

  assign RegWrOp[1] = JAL;
endmodule

module IFU (
  input  clk,
  input  rst,
  input  [1:0] NPCOp,
  input  [31:0] imm,
  input  [25:0] instr_index,
  output [31:0] PC_4,
  output [31:0] inStr,
  output [31:0] out_8
);

  wire comparator_1_eq;
  wire [11:0] subtractor_1_out;
  wire [15:0] shifter_1_out;
  wire [31:0] adder_2_out, bit_extender_1_out, NPC, register_1_q;

  Shifter #(.width(16)) shifter_1 (.in(imm[15:0]), .\dist (4'b0010), .out(shifter_1_out));
  Register #(.width(32)) register_1 (.D(NPC), .Q(register_1_q), .clk(clk), .clr(rst));  // open: en
  assign bit_extender_1_out = {{16{shifter_1_out[15]}}, shifter_1_out};  // Bit_Extender bit_extender_1
  Adder #(.width(32)) adder_1 (.a(32'h4), .b(out_8), .out(PC_4));  // open: cin, cout
  Adder #(.width(32)) adder_2 (.a(PC_4), .b(bit_extender_1_out), .out(adder_2_out));  // open: cin, cout
  Comparator #(.width(32)) comparator_1 (.a(register_1_q), .b({32{1'b0}}), .eq(comparator_1_eq));  // open: gt, lt
  Multiplexer #(.width(32)) multiplexer_1 (
    .in0(register_1_q), .in1(32'h3000), .out(out_8), .sel(comparator_1_eq));  // open: en
  // Probe on subtractor_1_out
  // Probe on NPC
  Multiplexer #(.select(2), .width(32)) multiplexer_2 (
    .in0(PC_4), .in1(adder_2_out), .in2({out_8[31:28], instr_index, 2'b00}), .out(NPC), .sel(NPCOp));  // open: in3, en
  Subtractor #(.width(12)) subtractor_1 (.a(out_8[13:2]), .b(12'hc00), .out(subtractor_1_out));  // open: bin, bout
  // Probe on out_8
  ROM #(.addrWidth(12), .dataWidth(32)) rom_1 (.addr(subtractor_1_out), .data(inStr));  // open: sel

  // Other names for the same wires on the sheet: instr_index_25[25:0] = instr_index; PC[31:0] = out_8;
  //   imm32[31:0] = imm; reset = rst

  // Notes on the sheet:
  //   PC + 4
  //   BEQ
  //   JAL
  //   contents of rom_1 (hex, n*v repeats v):
  //   3400000c 34010005 34020003 34030005 34040003 34050007 3406000a 34070008 3408000a 34090003 340a000b
  //   340b0008 340c0004 340d0009 340e000c 340f000b 3410000a 34110005 34120005 34130008 34140005 34150007
  //   34160009 34170006 34180009 34190008 341a0007 341b0006 341c000c 341d0003 341e0004 34030014 ac7b000c
  //   c000c27 0 34030010 ac7b0050 c000cae 0 3c05ffff 34a50001 3c05ffff 34a5ffff 34a50002 34050006 34050007
  //   3c14ffff 36940002 3c12ffff 3652fffe 3c0bffff 356bfffe 2925820 3414000a 34120009 340b0007 34030018
  //   ac6900a0 34130018 8e710010 3c0dffff 35adfffe 3c19ffff 37390000 372d0000 340d000c 34190005 3c0bffff
  //   356b0001 3c09ffff 35290003 3c10ffff 3610fffd 1698020 340b000a 34090005 34100006 3c18ffff 37180003
  //   3c12ffff 36520002 3c16ffff 36d60001 312b022 34180009 34120008 34160009 3c0effff 35ce0000 3c0fffff
  //   35ef0003 3c04ffff 3484fffe 1cf2022 340e000c 340f0009 3404000a 3c16ffff 36d60003 3c08ffff 35080002
  //   35160001 34160007 34080007 0 3c04ffff 34840003 3c08ffff 3508fffe 3c08ffff 35080000 884022 3404000a
  //   34080004 34080005 3c09ffff 35290003 3c17ffff 36f70002 36e90001 34090008 34170005 34110010 ae26008c
  //   34020010 8c57006c 0 34160018 aecf0054 3c03ffff 34630003 3c0affff 354afffd 3c12ffff 3652ffff 6a9022
  //   3403000c 340a0008 34120005 34170018 8ee60000 0 0 0 3409000c 8d270010 340f0014 adf0002c 3c1600a0 0 0
  //   3c08ffff 35080003 3c1bffff 377b0002 3768fffe 34080009 341b000b 3c00ffff 34000001 3c10ffff 3610fffd
  //   3c0dffff 35ad0001 106822 34000007 3410000a 340d000c 34040004 ac85002c 34060018 8cd40088 12a8ff76 0
  //   c000cb4 0 34080010 8d15005c c000d06 0 3c08ffff 35080003 3c1fffff 37ff0002 3c0effff 35ce0003 11f7020
  //   3408000b 341f0004 340e0009 340a000c ad410008 34120008 ae42004c 3c02ffff 34420002 3c02fffd 34020005
  //   3c03ffff 34630001 3c11ffff 3631ffff 3623fffd 3403000b 34110004 34040008 ac960060 3c1effff 37defffe
  //   3c1e0001 341e0009 0 3c1fffff 37ff0003 3c0affff 354a0000 355fffff 341f0005 340a000c 2024820 3c1affff
  //   375a0002 3c1affff 341a0007 340c0004 8d960058 3408000c 8d19007c 0 340a0010 ad48004c 0 1bd7022 0
  //   34160014 aec90038 120a022 3c1effff 37defffe 3c1e0002 341e0006 0 3c1500a7 0 3c00ffff 3400fffd
  //   3c1effff 37de0000 3c06ffff 34c6ffff 1e3020 34000003 341e0006 34060006 3c050057 3c0b002b 341c0008
  //   af900014 3c110050 1491822 12bdffab 0 c000d0b 0 3b51822 c000d70 0 333c822 340e0004 8dc10080 209c022
  //   3c0cffff 358cfffd 3c0c0000 340c000a 17d9022 341a0004 af580078 3024820 3c09ffff 35290003 3c1affff
  //   375a0002 3c00ffff 3400fffe 13a0020 3409000b 341a0009 3400000b 2e72822 3c04ffff 3484fffe 3c14ffff
  //   36940003 3c05ffff 34a50003 942822 3404000a 34140003 34050003 19be020 3c060087 3c01ffff 3421fffe
  //   3c09ffff 3529fffe 3521ffff 3401000b 3409000c 341a0008 af590034 1ace020 3c16ffff 36d60000 3c160002
  //   34160006 863022 340b0014 ad790098 341b0018 8f720084 0 0 3c12ffff 3652ffff 3c01ffff 3421fffe 3c18ffff
  //   37180000 241c022 3412000a 34010008 34180004 3c08ffff 35080002 3c0fffff 35ef0002 35e8fffe 34080008
  //   340f0009 26cf822 340b000c ad700058 0 0 3c16ffff 36d60002 3c10ffff 3610fffe 3c15ffff 36b50003 2d0a822
  //   34160003 34100007 34150004 26a9820 3c1dffff 37bd0003 3c0cffff 358c0002 3c15ffff 36b5ffff 3aca822
  //   341d0003 340c000b 34150004 1109ff99 0 13520051 0 34080004 8d120074 3c00ffff 34000001 3c1fffff
  //   37ff0002 37e00001 34000003 341f000b 0 34010010 ac240050 0 368a0043 341a0004 8f5a00a0 341b0014
  //   af7d0028 34060008 acd80058 34000008 8c1e0018 3c0dffff 35ad0001 3c14ffff 36940003 368dffff 340d0004
  //   34140008 1cf022 3c01ffff 34210002 3c15ffff 36b50000 3c00ffff 3400fffe 350020 34010004 34150007
  //   34000007 3c1200c6 341f0008 8ff00070 341e000c afcd0048 1885820 3fff022 34120008 ae4b0050 0 0 34020010
  //   ac430080 8aa820 3c00ffff 34000002 3c00fffe 34000004 3c1cffff 379c0002 3c19ffff 37390003 373c0003
  //   341c0007 34190007 3c10ffff 3610fffe 3c08ffff 3508fffe 3510fffe 3410000c 3408000b 0 34170010 aeeb0040
  //   341b0008 af690060 2f6b820 12a00001 0 23c5020 0 341c0010 af8e004c 3c1f002e 340d000c 8db9009c 341e0018
  //   8fd70018 e6f820 3c05ffff 34a5fffe 3c04ffff 34840000 3c0affff 354afffe a45020 34050007 34040004
  //   340a0006 3c00ffff 34000003 3c16ffff 36d6fffd 36c00002 34000009 34160005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
endmodule

module GRF (
  input  clk,
  input  reset,
  input  WE,
  input  [4:0] A1,
  input  [4:0] A2,
  input  [4:0] A3,
  input  [31:0] WD,
  output [31:0] out_8,
  output [31:0] out_9
);

  wire [31:0] out00, out01, out02, out03, out04, out05, out06, out07, out08, out09, out10, out11, out12,
       out13, out14, out15, out16, out17, out18, out19, out20, out21, out22, out23, out24, out25, out26,
       out27, out28, out29, out30, out31, wr01, wr02, wr03, wr04, wr05, wr06, wr07, wr08, wr09, wr10, wr11,
       wr12, wr13, wr14, wr15, wr16, wr17, wr18, wr19, wr20, wr21, wr22, wr23, wr24, wr25, wr26, wr27, wr28,
       wr29, wr30, wr31;

  Multiplexer #(.select(5), .width(32)) multiplexer_1 (
    .in0(out00), .in1(out01), .in2(out02), .in3(out03), .in4(out04), .in5(out05), .in6(out06), .in7(out07),
    .in8(out08), .in9(out09), .in10(out10), .in11(out11), .in12(out12), .in13(out13), .in14(out14),
    .in15(out15), .in16(out16), .in17(out17), .in18(out18), .in19(out19), .in20(out20), .in21(out21),
    .in22(out22), .in23(out23), .in24(out24), .in25(out25), .in26(out26), .in27(out27), .in28(out28),
    .in29(out29), .in30(out30), .in31(out31), .out(out_9), .sel(A2));  // open: en
  Register #(.width(32)) register_1 (.D({32{1'b0}}), .en(WE), .Q(out00), .clk(clk), .clr(reset));
  Register #(.width(32)) register_2 (.D(wr08), .en(WE), .Q(out08), .clk(clk), .clr(reset));
  Register #(.width(32)) register_3 (.D(wr16), .en(WE), .Q(out16), .clk(clk), .clr(reset));
  Register #(.width(32)) register_4 (.D(wr24), .en(WE), .Q(out24), .clk(clk), .clr(reset));
  Register #(.width(32)) register_5 (.D(wr01), .en(WE), .Q(out01), .clk(clk), .clr(reset));
  Register #(.width(32)) register_6 (.D(wr09), .en(WE), .Q(out09), .clk(clk), .clr(reset));
  Register #(.width(32)) register_7 (.D(wr17), .en(WE), .Q(out17), .clk(clk), .clr(reset));
  Register #(.width(32)) register_8 (.D(wr25), .en(WE), .Q(out25), .clk(clk), .clr(reset));
  Register #(.width(32)) register_9 (.D(wr02), .en(WE), .Q(out02), .clk(clk), .clr(reset));
  Register #(.width(32)) register_10 (.D(wr10), .en(WE), .Q(out10), .clk(clk), .clr(reset));
  Register #(.width(32)) register_11 (.D(wr18), .en(WE), .Q(out18), .clk(clk), .clr(reset));
  Register #(.width(32)) register_12 (.D(wr26), .en(WE), .Q(out26), .clk(clk), .clr(reset));
  Register #(.width(32)) register_13 (.D(wr03), .en(WE), .Q(out03), .clk(clk), .clr(reset));
  Register #(.width(32)) register_14 (.D(wr11), .en(WE), .Q(out11), .clk(clk), .clr(reset));
  Register #(.width(32)) register_15 (.D(wr19), .en(WE), .Q(out19), .clk(clk), .clr(reset));
  Register #(.width(32)) register_16 (.D(wr27), .en(WE), .Q(out27), .clk(clk), .clr(reset));
  Multiplexer #(.select(5), .width(32)) multiplexer_2 (
    .in0(out00), .in1(out01), .in2(out02), .in3(out03), .in4(out04), .in5(out05), .in6(out06), .in7(out07),
    .in8(out08), .in9(out09), .in10(out10), .in11(out11), .in12(out12), .in13(out13), .in14(out14),
    .in15(out15), .in16(out16), .in17(out17), .in18(out18), .in19(out19), .in20(out20), .in21(out21),
    .in22(out22), .in23(out23), .in24(out24), .in25(out25), .in26(out26), .in27(out27), .in28(out28),
    .in29(out29), .in30(out30), .in31(out31), .out(out_8), .sel(A1));  // open: en
  Register #(.width(32)) register_17 (.D(wr04), .en(WE), .Q(out04), .clk(clk), .clr(reset));
  Register #(.width(32)) register_18 (.D(wr12), .en(WE), .Q(out12), .clk(clk), .clr(reset));
  Register #(.width(32)) register_19 (.D(wr20), .en(WE), .Q(out20), .clk(clk), .clr(reset));
  Register #(.width(32)) register_20 (.D(wr28), .en(WE), .Q(out28), .clk(clk), .clr(reset));
  // Probe on wr01
  Demultiplexer #(.select(5), .width(32), .tristate("true")) demultiplexer_1 (
    .out1(wr01), .out2(wr02), .out3(wr03), .out4(wr04), .out5(wr05), .out6(wr06), .out7(wr07), .out8(wr08),
    .out9(wr09), .out10(wr10), .out11(wr11), .out12(wr12), .out13(wr13), .out14(wr14), .out15(wr15),
    .out16(wr16), .out17(wr17), .out18(wr18), .out19(wr19), .out20(wr20), .out21(wr21), .out22(wr22),
    .out23(wr23), .out24(wr24), .out25(wr25), .out26(wr26), .out27(wr27), .out28(wr28), .out29(wr29),
    .out30(wr30), .out31(wr31), .in(WD), .sel(A3));  // open: out0, en
  Register #(.width(32)) register_21 (.D(wr05), .en(WE), .Q(out05), .clk(clk), .clr(reset));
  Register #(.width(32)) register_22 (.D(wr13), .en(WE), .Q(out13), .clk(clk), .clr(reset));
  Register #(.width(32)) register_23 (.D(wr21), .en(WE), .Q(out21), .clk(clk), .clr(reset));
  Register #(.width(32)) register_24 (.D(wr29), .en(WE), .Q(out29), .clk(clk), .clr(reset));
  Register #(.width(32)) register_25 (.D(wr06), .en(WE), .Q(out06), .clk(clk), .clr(reset));
  Register #(.width(32)) register_26 (.D(wr14), .en(WE), .Q(out14), .clk(clk), .clr(reset));
  Register #(.width(32)) register_27 (.D(wr22), .en(WE), .Q(out22), .clk(clk), .clr(reset));
  Register #(.width(32)) register_28 (.D(wr30), .en(WE), .Q(out30), .clk(clk), .clr(reset));
  Register #(.width(32)) register_29 (.D(wr07), .en(WE), .Q(out07), .clk(clk), .clr(reset));
  Register #(.width(32)) register_30 (.D(wr15), .en(WE), .Q(out15), .clk(clk), .clr(reset));
  Register #(.width(32)) register_31 (.D(wr23), .en(WE), .Q(out23), .clk(clk), .clr(reset));
  Register #(.width(32)) register_32 (.D(wr31), .en(WE), .Q(out31), .clk(clk), .clr(reset));

  // Other names for the same wires on the sheet: RD1[31:0] = out_8; RD2[31:0] = out_9
endmodule

module ALU (
  input  [1:0] ALUOp,
  input  [31:0] SrcA,
  input  [31:0] SrcB,
  output zero,
  output [31:0] out_5
);

  wire [31:0] adder_1_out, or_1_out, shifter_1_out, subtractor_1_out;

  Adder #(.width(32)) adder_1 (.a(SrcA), .b(SrcB), .out(adder_1_out));  // open: cin, cout
  Subtractor #(.width(32)) subtractor_1 (.a(SrcA), .b(SrcB), .out(subtractor_1_out));  // open: bin, bout
  assign or_1_out = SrcA | SrcB;  // OR_Gate or_1, 32 bits wide
  Shifter #(.width(32)) shifter_1 (.in(SrcA), .\dist (SrcB[4:0]), .out(shifter_1_out));
  Multiplexer #(.select(2), .width(32)) multiplexer_1 (
    .in0(adder_1_out), .in1(subtractor_1_out), .in2(or_1_out), .in3(shifter_1_out), .out(out_5), .sel(ALUOp));  // open: en
  Comparator #(.width(32)) comparator_1 (.a(out_5), .b({32{1'b0}}), .eq(zero));  // open: gt, lt
endmodule

module EXT (
  input  EXTOp,
  input  [15:0] in_2,
  output [31:0] out_3
);

  wire [31:0] bit_extender_1_out, bit_extender_2_out;

  assign bit_extender_1_out = {{16{1'b0}}, in_2};  // Bit_Extender bit_extender_1
  assign bit_extender_2_out = {{16{in_2[15]}}, in_2};  // Bit_Extender bit_extender_2
  Multiplexer #(.width(32)) multiplexer_1 (
    .in0(bit_extender_1_out), .in1(bit_extender_2_out), .out(out_3), .sel(EXTOp));  // open: en
endmodule

module DM (
  input  [31:0] Address,
  input  [31:0] WD,
  input  clk,
  input  reset,
  input  MemWrite,
  output [31:0] RD
);

  // Probe on Address[13:0]
  RAM #(.addrWidth(14), .dataWidth(32), .bus("separate")) ram_1 (
    .addr(Address[13:0]), .din(WD), .data(RD), .str(MemWrite), .clk(clk), .clr(reset));  // open: sel, ld

  // Other names for the same wires on the sheet: WE = MemWrite

  // Notes on the sheet:
  //   WD: 32bits
  //   Adress: 14bits 
endmodule

module NPCOp (
  input  BEQ,
  input  zero,
  input  JAL,
  output [1:0] NPCOp
);

  and and_1 (NPCOp[0], BEQ, zero);

  assign NPCOp[1] = JAL;
endmodule
